# Fritzing sketch leftmotor (saved by Fritzing 0.9.2b)

parts:
  Part1 = Arduino Leonardo (Rev3b)
  X2 = X113647 Stepper Driver Board [package=board]

nets:
  N1: Part1.D7, X2.IN4
  N2: Part1.5V, X2.+V
  N3: Part1.D8/A8, X2.IN3
  N4: Part1.D9_PWM/A9, X2.IN2
  N5: Part1.D10_PWM/A10, X2.IN1
  GND: Part1.GND, X2.GND

custom parts:
  X113647 Stepper Driver Board: A common stepper motor driver board based on ULN2003APG darlington array
