# Fritzing sketch oledwiring (saved by Fritzing 0.9.2b)

parts:
  o1 = Module display OLED I2C 128x64 SSD1306 [package=THT]
  Part1 = Arduino Leonardo (Rev3b)

nets:
  GND: o1.GND, Part1.GND
  VCC: o1.VCC, Part1.3V3
  N1: o1.SCL, Part1.A5
  N2: o1.SDA, Part1.A4

custom parts:
  Module display OLED I2C 128x64 SSD1306: Ecran OLED I2C SSD163 de 128x64 avec connexion I2C
