# Fritzing sketch rightmotor (saved by Fritzing 0.9.2b)

parts:
  Part1 = Arduino Leonardo (Rev3b)
  X1 = X113647 Stepper Driver Board [package=board]

nets:
  N1: Part1.D0/RX, X1.IN4
  N2: Part1.D2/SDA, X1.IN3
  N3: Part1.D5_PWM, X1.IN2
  N4: Part1.D6_PWM/A7, X1.IN1
  GND: Part1.GND, X1.GND
  N5: Part1.VIN, X1.+V

custom parts:
  X113647 Stepper Driver Board: A common stepper motor driver board based on ULN2003APG darlington array
